# Fritzing sketch Lamp (saved by Fritzing 0.8.7b)
circuit board: 8.46667cm x 5.64444cm
breadboards: 1

parts:
  Arduino = Arduino Uno (Rev3)
  RN-42XV = Bluetooth Module Breakout - Roving Networks (RN-41)
  R2 = Resistor [tolerance=±5% resistance=10k package=THT]
  R3 = Resistor [tolerance=±5% resistance=10k package=THT]
  LED-Strip = Header 4 [package=jst-4-pth]
  PD139 = npn-Powertransistor [package="TO220 [THT]"]
  PD139_2 = npn-Powertransistor [package="TO220 [THT]"]
  J2 = Power Jack [package=power_jack_pth_lock]
  R1 = Resistor [tolerance=±5% resistance=10k package=THT]
  PD139_3 = npn-Powertransistor [package="TO220 [THT]"]

nets:
  GND: Arduino.GND, RN-42XV.GND, PD139.emitter, PD139_2.emitter, J2.GND, PD139_3.emitter
  N1: Arduino.D2, RN-42XV.UARTRX
  N2: Arduino.D3_PWM, R3.Pin_0
  N3: Arduino.D4, RN-42XV.UARTTX
  N4: Arduino.D5_PWM, Arduino.D6_PWM, R2.Pin_0, R1.Pin_0
  3V3: Arduino.3V3, RN-42XV.VCC
  N5: Arduino.VIN, LED-Strip.4, J2.PWR
  N6: R2.Pin_1, PD139_3.base
  N7: R3.Pin_1, PD139.base
  N8: LED-Strip.1, PD139.collector
  N9: LED-Strip.2, PD139_2.collector
  N10: LED-Strip.3, PD139_3.collector
  N11: PD139_2.base, R1.Pin_1
